// Logisim project cpu.circ as structural Verilog: 1 circuit, main circuit cpu
module cpu (
);

  wire ALU_Src, Main_Clock, Reg_Write, RegisterFile_p5, Zero;
  wire [1:0] MEMW_Sel, PC_control, Reg_Dest, Reg_Write_Sel, Shift_Select;
  wire [3:0] decoder_1_out0, multiplexer_6_out;
  wire [4:0] ALU_Ctrl, multiplexer_2_out, multiplexer_5_out;
  wire [5:0] Func, opcode;
  wire [15:6] Imm;
  wire [25:16] J_ADD;
  wire [27:0] PC;
  wire [31:0] ALU_Result, Imm_ext, J_value, MemReadData, multiplexer_3_out, multiplexer_4_out, newPC, PC_4,
       PC_4_Imm, Read_Data1, Read_Data2, shifter_1_out;

  Clock clock_1 (.out(Main_Clock));
  Register #(.width(32)) u_PC (.D(newPC), .en(1'b1), .Q({J_value[31:28], PC}));  // open: clk, clr
  Shifter #(.width(32)) shifter_1 (.in(Imm_ext), .\dist (5'b00010), .out(shifter_1_out));
  Multiplexer #(.select(2), .width(32)) multiplexer_1 (
    .in0(PC_4), .in1(PC_4_Imm), .in2(J_value), .in3(Read_Data1), .out(newPC), .sel(PC_control));
  Adder #(.width(32)) adder_1 (.a({J_value[31:28], PC}), .b(32'h4), .out(PC_4));  // open: cin, cout
  Adder #(.width(32)) adder_2 (.a(PC_4), .b(shifter_1_out), .out(PC_4_Imm));  // open: cin, cout
  Shifter #(.width(28)) shifter_2 (.in({2'b00, J_ADD, Imm, Func}), .\dist (5'b00010), .out(J_value[27:0]));
  mem InstMem (
    .MemAddress({J_value[31:28], PC}), .MemWriteMask(4'b0000), .MemWriteData({32{1'b1}}), .clk(Main_Clock),
    .MemReadData({opcode, J_ADD, Imm, Func}));
  control_unit CU (
    .opcode(opcode), .func(Func), .Reg_Write(Reg_Write), .ALU_Src(ALU_Src), .PC_control(PC_control),
    .Reg_Dest_Sel(Reg_Dest), .Reg_Write_Sel(Reg_Write_Sel), .MEMW_Sel(MEMW_Sel));
  assign Imm_ext = {{16{Imm[15]}}, {Imm, Func}};  // Bit_Extender bit_extender_1
  Multiplexer #(.select(2), .width(5)) multiplexer_2 (
    .in0(J_ADD[20:16]), .in1(Imm[15:11]), .in2({5{1'b1}}), .in3(5'b00001), .out(multiplexer_2_out),
    .sel(Reg_Dest));
  Multiplexer #(.select(2), .width(32)) multiplexer_3 (
    .in0(ALU_Result), .in1(MemReadData), .in2({J_value[31:28], PC}), .in3({32{1'b0}}),
    .out(multiplexer_3_out), .sel(Reg_Write_Sel));
  Multiplexer #(.width(32)) multiplexer_4 (.in0(Read_Data2), .in1(Imm_ext), .out(multiplexer_4_out), .sel(ALU_Src));
  // regfile RegisterFile: pin names not known; wires that end beside it: J_ADD[25:21], J_ADD[20:16], multiplexer_2_out, multiplexer_3_out, RegisterFile_p5, Main_Clock, Read_Data1, Read_Data2
  Multiplexer #(.select(2), .width(5)) multiplexer_5 (
    .in0(Imm[10:6]), .in1(Read_Data1[4:0]), .in2(5'b10000), .in3({5{1'b0}}), .out(multiplexer_5_out),
    .sel(Shift_Select));
  ALU ArithLogicUnit (
    .Input1(Read_Data1), .Input2(multiplexer_4_out), .op(ALU_Ctrl), .SHA(multiplexer_5_out), .Zero(Zero),
    .Result(ALU_Result));
  Decoder #(.enable("false"), .select(2)) decoder_1 (
    .out0(decoder_1_out0[0]), .out1(decoder_1_out0[1]), .out2(decoder_1_out0[2]), .out3(decoder_1_out0[3]),
    .sel(ALU_Result[1:0]));
  Multiplexer #(.select(2), .width(4)) multiplexer_6 (
    .in0(4'b0000), .in1(4'b1111), .in2(decoder_1_out0), .in3(4'b0000), .out(multiplexer_6_out), .sel(MEMW_Sel));
  alu_control_unit ALU_Control (.func(Func), .opcode(opcode), .ALU_control_bits(ALU_Ctrl), .Shift_Select(Shift_Select));
  mem DataMem (
    .MemAddress(ALU_Result), .MemWriteMask(multiplexer_6_out), .MemWriteData(Read_Data2), .clk(Main_Clock),
    .MemReadData(MemReadData));

  // Other names for the same wires on the sheet: Imm[5:0] = Func; J_ADD[15:0] = {Imm, Func}; SHA[4:0] = Imm[10:6];
  //   rd[4:0] = Imm[15:11]; rt[4:0] = J_ADD[20:16]; rs[4:0] = J_ADD[25:21]; PC[31:28] = J_value[31:28]

  // Notes on the sheet:
  //   JR
  //   PC Logic
  //   Clock
  //   Next
  //   Branch
  //   Jump
endmodule
